# Fritzing sketch Schaltung (saved by Fritzing 0.9.2b)
stripboards: 1

parts:
  Raspberry_Pi1 = Raspberry Pi 2
  J3 = male pin header, 3 pins [form="♂ (male)"]
  R2 = Resistor [tolerance=±5% resistance=1k package="2010 [SMD]"]
  J2 = male pin header, 6 pins [form="♂ (male)"]
  R1 = Resistor [tolerance=±5% resistance=10k package="2010 [SMD]"]
  J4 = male pin header, 2 pins [form="♂ (male)"]
  J5 = male pin header, 3 pins [form="♂ (male)"]
  J6 = male pin header, 3 pins [form="♂ (male)"]
  LCD1 = LCD_Display
  J1 = male alternating pin header, 7 pins [form="♂ (male)"]

nets:
  N1: Raspberry_Pi1.3v3, J3.pin2, R1.Pin_1, J4.pin1, J1.pin3
  N2: Raspberry_Pi1.GPIO2, J3.pin3, J1.pin4
  N3: Raspberry_Pi1.GPIO17, J4.pin2, J1.pin5
  N4: Raspberry_Pi1.GPIO27, J6.pin3, J1.pin7
  N5: Raspberry_Pi1.GPIO10, LCD1.connector15
  N6: Raspberry_Pi1.GPIO9, LCD1.connector14
  N7: Raspberry_Pi1.GPIO11, LCD1.connector13
  N8: Raspberry_Pi1.GPIO5, LCD1.connector12
  N9: Raspberry_Pi1.GPIO6, LCD1.connector11
  N10: Raspberry_Pi1.GPIO13, LCD1.connector10
  N11: Raspberry_Pi1.GPIO19, LCD1.connector9
  N12: Raspberry_Pi1.GPIO26, LCD1.connector8
  N13: Raspberry_Pi1.GPIO21, LCD1.connector5
  N14: Raspberry_Pi1.GPIO20, LCD1.connector7
  N15: Raspberry_Pi1.GND, J3.pin1, R2.Pin_1, J2.pin4, J2.pin5, J2.pin6, J5.pin1, J6.pin1, LCD1.connector1, LCD1.connector2, LCD1.connector6, J1.pin1
  N16: Raspberry_Pi1.GPIO18, J5.pin3, J1.pin6
  N17: Raspberry_Pi1.5V, J2.pin2, J2.pin3, J5.pin2, J6.pin2, LCD1.connector0, LCD1.connector3, J1.pin2
  N18: R2.Pin_0, J2.pin1, R1.Pin_0, LCD1.connector4

notes:
  PWM
  Br1
  GND
  3.3V
  5V
  T
  Br2
